# Fritzing sketch four_digits_binary_counter (saved by Fritzing 0.7.10b)
breadboards: 1

parts:
  Arduino1 = Arduino
  U1 = 74HC595 [package="DIP16 [THT]"]
  U2 = mystery part, 12 pins [chip_label=" 4 Digits 7 Segments Display"]

nets:
  N1: Arduino1.D12, U1.SH_CP
  N2: Arduino1.D11, U1.DS
  N3: Arduino1.D8, U1.ST_CP
  +5V: Arduino1.+5V, U1.MR, U1.VCC
  GND: Arduino1.GND, U1.GND, U1.OE
  N4: Arduino1.A0, U2.pin12
  N5: Arduino1.A1, U2.pin9
  N6: Arduino1.A2, U2.pin8
  N7: Arduino1.A3, U2.pin6
  N8: U1.Q1, U2.pin5
  N9: U1.Q2, U2.pin10
  N10: U1.Q3, U2.pin1
  N11: U1.Q4, U2.pin2
  N12: U1.Q5, U2.pin4
  N13: U1.Q6, U2.pin7
  N14: U1.Q7, U2.pin11
  N15: U1.Q0, U2.pin3

notes:
  Y1 a f 2Y 3Y b
  4 Digits 7 Segments Display
  e d dp c g 4Y
  using analog pins as digit pins
