# Fritzing sketch four_digits_connection (saved by Fritzing 0.7.10b)
breadboards: 1

parts:
  Arduino1 = Arduino
  U1 = mystery part, 12 pins [chip_label="4 Digits 7 Segments Display"]

nets:
  N1: Arduino1.D12, U1.pin3
  N2: Arduino1.D8, U1.pin5
  N3: Arduino1.D7, U1.pin10
  N4: Arduino1.D6, U1.pin1
  N5: Arduino1.D5, U1.pin2
  N6: Arduino1.D4, U1.pin4
  N7: Arduino1.D3, U1.pin7
  N8: Arduino1.D2, U1.pin11
  N9: Arduino1.A0, U1.pin12
  N10: Arduino1.A1, U1.pin9
  N11: Arduino1.A2, U1.pin8
  N12: Arduino1.A3, U1.pin6

notes:
  You can use analog pins as digit pins
