# Fritzing sketch one_digit_binary_counter (saved by Fritzing 0.7.10b)
breadboards: 2

parts:
  U1 = 74HC595 [package="DIP16 [THT]"]
  U2 = mystery part, 10 pins [chip_label=?]
  Adafruit_Atmega32u1 = Adafruit Atmega32u4 Breakout Board [part_number="Atmega 32u4"]

nets:
  N1: U1.Q1, U2.pin10
  N2: U1.Q2, U2.pin9
  N3: U1.Q3, U2.pin1
  N4: U1.Q4, U2.pin2
  N5: U1.Q5, U2.pin4
  N6: U1.Q6, U2.pin6
  N7: U1.Q7, U2.pin7
  N8: U1.GND, U2.pin3
  N9: U1.MR, U1.VCC
  N10: U1.SH_CP, Adafruit_Atmega32u1.D6
  N11: U1.ST_CP, Adafruit_Atmega32u1.D5
  N12: U1.OE, U2.pin8
  N13: U1.DS, Adafruit_Atmega32u1.D3
  N14: U1.Q0, U2.pin5
