# Fritzing sketch hardware_debounce (saved by Fritzing 0.7.10b)
breadboards: 1

parts:
  S1 = Pushbutton [package="[THT]"]
  R1 = Resistor [tolerance=±1% resistance=10k package=THT]
  C1 = Electrolytic Capacitor [capacitance=10µF voltage=20V package="100 mil [THT, electrolytic]"]
  LED1 = LED - 5mm [color="Blue (470nm)" package="5 mm [THT]"]
  U1 = mystery part, 14 pins [chip_label=74AC14N]
  VCC1 = 4 x AAA Battery Mount

nets:
  N1: S1.Pin_1, S1.Pin_2, C1.+, LED1.cathode, U1.pin7, VCC1.-
  N2: S1.Pin_3, S1.Pin_4, R1.Pin_1, C1.-, U1.pin1
  N3: R1.Pin_0, U1.pin14, VCC1.+
  N4: LED1.anode, U1.pin2
