# Fritzing sketch lm35 (saved by Fritzing 0.7.10b)
breadboards: 1

parts:
  T1 = LM35 Temperature Sensor [package="TO92 [THT]"]
  Arduino1 = Arduino

nets:
  N1: T1.+Vs, Arduino1.+5V
  N2: T1.Vout, Arduino1.A0
  GND: T1.GND, Arduino1.GND
